// Digital circuit 74269.dig as structural Verilog
module _74269 (
  input  D0,
  input  D1,
  input  D2,
  input  D4,
  input  D3,
  input  D5,
  input  D6,
  input  D7,
  input  nPE,
  input  CP,
  input  U_nD,
  input  nCEP,
  input  nCET,
  output nTC,
  output Q7,
  output Q6,
  output Q5,
  output Q4,
  output Q3,
  output Q2,
  output Q1,
  output Q0
);

  wire _74269_detail_1_nq, _74269_detail_1_q, _74269_detail_2_nq, _74269_detail_2_q, _74269_detail_3_nq,
       _74269_detail_3_q, _74269_detail_4_nq, _74269_detail_4_q, _74269_detail_5_nq, _74269_detail_5_q,
       _74269_detail_6_nq, _74269_detail_6_q, _74269_detail_7_nq, _74269_detail_7_q, _74269_detail_8_nq,
       _74269_detail_8_q, and_1_out, and_2_out, and_3_out, and_4_out, and_5_out, and_6_out, and_7_out,
       and_8_out, and_9_out, and_10_out, and_11_out, and_12_out, and_13_out, and_14_out, and_15_out,
       and_16_out, and_17_out, and_18_out, and_19_out, nor_1_out, nor_2_out, nor_3_out, nor_4_out, nor_5_out,
       nor_6_out, nor_7_out, nor_8_out, not_1_out, not_2_out, not_3_out, not_4_out, not_5_out, not_6_out;

  not not_1 (not_1_out, nPE);
  not not_2 (not_2_out, CP);
  not not_3 (not_3_out, U_nD);
  not not_4 (not_4_out, nCEP);
  not not_5 (not_5_out, nCET);
  _74269_detail _74269_detail_1 (
    .Dn(D0), .PE(not_1_out), .nTOGGLE(nor_1_out), .nCP(not_2_out), .Q(_74269_detail_1_q),
    .nQ(_74269_detail_1_nq));
  _74269_detail _74269_detail_2 (
    .Dn(D1), .PE(not_1_out), .nTOGGLE(nor_2_out), .nCP(not_2_out), .Q(_74269_detail_2_q),
    .nQ(_74269_detail_2_nq));
  _74269_detail _74269_detail_3 (
    .Dn(D2), .PE(not_1_out), .nTOGGLE(nor_3_out), .nCP(not_2_out), .Q(_74269_detail_3_q),
    .nQ(_74269_detail_3_nq));
  _74269_detail _74269_detail_4 (
    .Dn(D3), .PE(not_1_out), .nTOGGLE(nor_4_out), .nCP(not_2_out), .Q(_74269_detail_4_q),
    .nQ(_74269_detail_4_nq));
  _74269_detail _74269_detail_5 (
    .Dn(D4), .PE(not_1_out), .nTOGGLE(nor_5_out), .nCP(not_2_out), .Q(_74269_detail_5_q),
    .nQ(_74269_detail_5_nq));
  _74269_detail _74269_detail_6 (
    .Dn(D5), .PE(not_1_out), .nTOGGLE(nor_6_out), .nCP(not_2_out), .Q(_74269_detail_6_q),
    .nQ(_74269_detail_6_nq));
  _74269_detail _74269_detail_7 (
    .Dn(D6), .PE(not_1_out), .nTOGGLE(nor_7_out), .nCP(not_2_out), .Q(_74269_detail_7_q),
    .nQ(_74269_detail_7_nq));
  _74269_detail _74269_detail_8 (
    .Dn(D7), .PE(not_1_out), .nTOGGLE(nor_8_out), .nCP(not_2_out), .Q(_74269_detail_8_q),
    .nQ(_74269_detail_8_nq));
  not not_6 (not_6_out, not_3_out);
  and and_1 (and_1_out, not_4_out, not_5_out);
  nor nor_1 (nor_1_out, and_11_out, and_9_out);
  nor nor_2 (nor_2_out, and_12_out, and_2_out);
  nor nor_3 (nor_3_out, and_13_out, and_3_out);
  nor nor_4 (nor_4_out, and_14_out, and_4_out);
  nor nor_5 (nor_5_out, and_15_out, and_5_out);
  nor nor_6 (nor_6_out, and_16_out, and_6_out);
  nor nor_7 (nor_7_out, and_17_out, and_7_out);
  nor nor_8 (nor_8_out, and_18_out, and_8_out);
  and and_2 (and_2_out, _74269_detail_1_q, not_6_out, and_1_out);
  and and_3 (and_3_out, _74269_detail_1_q, _74269_detail_2_q, not_6_out, and_1_out);
  and and_4 (and_4_out, _74269_detail_1_q, _74269_detail_2_q, _74269_detail_3_q, not_6_out, and_1_out);
  and and_5 (and_5_out, _74269_detail_1_q, _74269_detail_2_q, _74269_detail_3_q, _74269_detail_4_q, not_6_out, and_1_out);
  and and_6 (and_6_out, _74269_detail_1_q, _74269_detail_2_q, _74269_detail_3_q, _74269_detail_4_q, _74269_detail_5_q, not_6_out, and_1_out);
  and and_7 (and_7_out, _74269_detail_1_q, _74269_detail_2_q, _74269_detail_3_q, _74269_detail_4_q, _74269_detail_5_q, _74269_detail_6_q, not_6_out, and_1_out);
  and and_8 (and_8_out, _74269_detail_1_q, _74269_detail_2_q, _74269_detail_3_q, _74269_detail_4_q, _74269_detail_5_q, _74269_detail_6_q, _74269_detail_7_q, not_6_out, and_1_out);
  and and_9 (and_9_out, not_6_out, and_1_out);
  and and_10 (and_10_out, not_5_out, _74269_detail_1_q, _74269_detail_2_q, _74269_detail_3_q, _74269_detail_4_q, _74269_detail_5_q, _74269_detail_6_q, _74269_detail_7_q, _74269_detail_8_q, not_6_out);
  and and_11 (and_11_out, and_1_out, not_3_out);
  and and_12 (and_12_out, and_1_out, _74269_detail_1_nq, not_3_out);
  and and_13 (and_13_out, _74269_detail_1_nq, _74269_detail_2_nq, not_3_out, and_1_out);
  and and_14 (and_14_out, _74269_detail_1_nq, _74269_detail_2_nq, _74269_detail_3_nq, not_3_out, and_1_out);
  and and_15 (and_15_out, _74269_detail_1_nq, _74269_detail_2_nq, _74269_detail_3_nq, _74269_detail_4_nq, not_3_out, and_1_out);
  and and_16 (and_16_out, _74269_detail_1_nq, _74269_detail_2_nq, _74269_detail_3_nq, _74269_detail_4_nq, _74269_detail_5_nq, not_3_out, and_1_out);
  and and_17 (and_17_out, _74269_detail_1_nq, _74269_detail_2_nq, _74269_detail_3_nq, _74269_detail_4_nq, _74269_detail_5_nq, _74269_detail_6_nq, not_3_out, and_1_out);
  and and_18 (and_18_out, _74269_detail_1_nq, _74269_detail_2_nq, _74269_detail_3_nq, _74269_detail_4_nq, _74269_detail_5_nq, _74269_detail_6_nq, _74269_detail_7_nq, not_3_out, and_1_out);
  and and_19 (and_19_out, _74269_detail_1_nq, _74269_detail_2_nq, _74269_detail_3_nq, _74269_detail_4_nq, _74269_detail_5_nq, _74269_detail_6_nq, _74269_detail_7_nq, _74269_detail_8_nq, not_3_out, not_5_out);
  not not_7 (Q0, _74269_detail_1_nq);
  not not_8 (Q1, _74269_detail_2_nq);
  not not_9 (Q2, _74269_detail_3_nq);
  not not_10 (Q3, _74269_detail_4_nq);
  not not_11 (Q4, _74269_detail_5_nq);
  not not_12 (Q5, _74269_detail_6_nq);
  not not_13 (Q6, _74269_detail_7_nq);
  not not_14 (Q7, _74269_detail_8_nq);
  nor nor_9 (nTC, and_19_out, and_10_out);

  // Notes on the sheet:
  //   D0: pin 23
  //   D1: pin 22
  //   D2: pin 21
  //   D4: pin 18
  //   D3: pin 20
  //   D5: pin 17
  //   D6: pin 16
  //   D7: pin 15
  //   nPE: pin 24
  //   CP: pin 11
  //   U_nD: pin 1
  //   nCEP: pin 12
  //   nCET: pin 13
  //   nTC: pin 14
  //   Q7: pin 10
  //   Q6: pin 9
  //   Q5: pin 8
  //   Q4: pin 6
  //   Q3: pin 5
  //   Q2: pin 4
  //   Q1: pin 3
  //   Q0: pin 2
  //   From https://www.mouser.co.uk/datasheet/2/302/74F269-351005.pdf
  //   With two corrections on TOGGLE input of D0 and D1
endmodule
