// Digital circuit 74299.dig as structural Verilog
module _74299 (
  input  SLSI,
  input  S0,
  input  S1,
  input  nCLK,
  input  SRSI,
  input  CLR,
  input  nG1,
  input  nG2,
  output A_Q_A,
  output B_Q_B,
  output C_Q_C,
  output D_Q_D,
  output E_Q_E,
  output F_Q_F,
  output G_Q_G,
  output H_Q_H,
  output Q_H,
  output Q_A
);

  wire and_1_out, and_2_out, and_3_out, and_4_out, and_5_out, and_6_out, and_7_out, and_8_out, and_9_out,
       and_10_out, and_11_out, and_12_out, and_13_out, and_14_out, and_15_out, and_16_out, and_17_out,
       and_18_out, and_19_out, and_20_out, and_21_out, and_22_out, and_23_out, and_24_out, and_25_out,
       and_26_out, and_27_out, and_28_out, and_29_out, and_30_out, and_31_out, and_32_out, and_33_out,
       d_ff_as_2_q, d_ff_as_3_q, d_ff_as_4_q, d_ff_as_5_q, d_ff_as_6_q, d_ff_as_7_q, d_ff_as_8_q, nor_1_out,
       not_1_out, not_2_out, not_3_out, not_4_out, not_5_out, not_7_out, or_1_out, or_2_out, or_3_out,
       or_4_out, or_5_out, or_6_out, or_7_out, or_8_out;

  not not_1 (not_1_out, S0);
  not not_2 (not_2_out, S1);
  not not_3 (not_3_out, not_1_out);
  not not_4 (not_4_out, not_2_out);
  not not_5 (not_5_out, CLR);
  not not_6 (Q_H, not_5_out);
  nor nor_1 (nor_1_out, ~S1, ~S0);  // NOr
  not not_7 (not_7_out, nCLK);
  and and_1 (and_1_out, ~nor_1_out, ~nG1, ~nG2);  // And
  and and_2 (and_2_out, not_2_out, not_3_out, SRSI);
  and and_3 (and_3_out, d_ff_as_2_q, not_1_out, not_4_out);
  assign A_Q_A = and_1_out ? Q_A : 1'bz;  // Driver driver_1
  and and_4 (and_4_out, A_Q_A, not_3_out, not_4_out);
  or or_1 (or_1_out, and_5_out, and_4_out, and_3_out, and_2_out);
  D_FF_AS d_ff_as_1 (.Set(1'b0), .D(or_1_out), .C(~not_7_out), .Clr(~Q_H), .Q(Q_A));  // open: nQ
  and and_5 (and_5_out, Q_A, not_1_out, not_2_out);
  and and_6 (and_6_out, not_2_out, not_3_out, Q_A);
  and and_7 (and_7_out, d_ff_as_3_q, not_1_out, not_4_out);
  assign B_Q_B = and_1_out ? d_ff_as_2_q : 1'bz;  // Driver driver_2
  and and_8 (and_8_out, B_Q_B, not_3_out, not_4_out);
  or or_2 (or_2_out, and_9_out, and_8_out, and_7_out, and_6_out);
  D_FF_AS d_ff_as_2 (.Set(1'b0), .D(or_2_out), .C(~not_7_out), .Clr(~Q_H), .Q(d_ff_as_2_q));  // open: nQ
  and and_9 (and_9_out, d_ff_as_2_q, not_1_out, not_2_out);
  and and_10 (and_10_out, not_2_out, not_3_out, d_ff_as_2_q);
  assign C_Q_C = and_1_out ? d_ff_as_3_q : 1'bz;  // Driver driver_3
  and and_11 (and_11_out, d_ff_as_4_q, not_1_out, not_4_out);
  or or_3 (or_3_out, and_13_out, and_12_out, and_11_out, and_10_out);
  and and_12 (and_12_out, C_Q_C, not_3_out, not_4_out);
  and and_13 (and_13_out, d_ff_as_3_q, not_1_out, not_2_out);
  D_FF_AS d_ff_as_3 (.Set(1'b0), .D(or_3_out), .C(~not_7_out), .Clr(~Q_H), .Q(d_ff_as_3_q));  // open: nQ
  and and_14 (and_14_out, not_2_out, not_3_out, d_ff_as_3_q);
  assign D_Q_D = and_1_out ? d_ff_as_4_q : 1'bz;  // Driver driver_4
  and and_15 (and_15_out, d_ff_as_5_q, not_1_out, not_4_out);
  and and_16 (and_16_out, D_Q_D, not_3_out, not_4_out);
  or or_4 (or_4_out, and_17_out, and_16_out, and_15_out, and_14_out);
  and and_17 (and_17_out, d_ff_as_4_q, not_1_out, not_2_out);
  D_FF_AS d_ff_as_4 (.Set(1'b0), .D(or_4_out), .C(~not_7_out), .Clr(~Q_H), .Q(d_ff_as_4_q));  // open: nQ
  and and_18 (and_18_out, not_2_out, not_3_out, d_ff_as_4_q);
  and and_19 (and_19_out, d_ff_as_6_q, not_1_out, not_4_out);
  assign E_Q_E = and_1_out ? d_ff_as_5_q : 1'bz;  // Driver driver_5
  and and_20 (and_20_out, E_Q_E, not_3_out, not_4_out);
  or or_5 (or_5_out, and_21_out, and_20_out, and_19_out, and_18_out);
  D_FF_AS d_ff_as_5 (.Set(1'b0), .D(or_5_out), .C(~not_7_out), .Clr(~Q_H), .Q(d_ff_as_5_q));  // open: nQ
  and and_21 (and_21_out, d_ff_as_5_q, not_1_out, not_2_out);
  and and_22 (and_22_out, not_2_out, not_3_out, d_ff_as_5_q);
  and and_23 (and_23_out, d_ff_as_7_q, not_1_out, not_4_out);
  assign F_Q_F = and_1_out ? d_ff_as_6_q : 1'bz;  // Driver driver_6
  and and_24 (and_24_out, F_Q_F, not_3_out, not_4_out);
  or or_6 (or_6_out, and_25_out, and_24_out, and_23_out, and_22_out);
  D_FF_AS d_ff_as_6 (.Set(1'b0), .D(or_6_out), .C(~not_7_out), .Clr(~Q_H), .Q(d_ff_as_6_q));  // open: nQ
  and and_25 (and_25_out, d_ff_as_6_q, not_1_out, not_2_out);
  and and_26 (and_26_out, not_2_out, not_3_out, d_ff_as_6_q);
  assign G_Q_G = and_1_out ? d_ff_as_7_q : 1'bz;  // Driver driver_7
  and and_27 (and_27_out, d_ff_as_8_q, not_1_out, not_4_out);
  or or_7 (or_7_out, and_29_out, and_28_out, and_27_out, and_26_out);
  and and_28 (and_28_out, G_Q_G, not_3_out, not_4_out);
  and and_29 (and_29_out, d_ff_as_7_q, not_1_out, not_2_out);
  D_FF_AS d_ff_as_7 (.Set(1'b0), .D(or_7_out), .C(~not_7_out), .Clr(~Q_H), .Q(d_ff_as_7_q));  // open: nQ
  and and_30 (and_30_out, not_2_out, not_3_out, d_ff_as_7_q);
  assign H_Q_H = and_1_out ? d_ff_as_8_q : 1'bz;  // Driver driver_8
  and and_31 (and_31_out, SLSI, not_1_out, not_4_out);
  and and_32 (and_32_out, H_Q_H, not_3_out, not_4_out);
  or or_8 (or_8_out, and_33_out, and_32_out, and_31_out, and_30_out);
  and and_33 (and_33_out, d_ff_as_8_q, not_1_out, not_2_out);
  D_FF_AS d_ff_as_8 (.Set(1'b0), .D(or_8_out), .C(~not_7_out), .Clr(~Q_H), .Q(d_ff_as_8_q));  // open: nQ

  // Notes on the sheet:
  //   A_Q_A: pin 7
  //   B_Q_B: pin 13
  //   C_Q_C: pin 6
  //   D_Q_D: pin 14
  //   E_Q_E: pin 5
  //   F_Q_F: pin 15
  //   G_Q_G: pin 4
  //   H_Q_H: pin 16
  //   Q_H: pin 17
  //   SLSI: pin 18
  //   S0: pin 1
  //   S1: pin 19
  //   nCLK: pin 12
  //   SRSI: pin 11
  //   CLR: pin 9
  //   nG1: pin 2
  //   nG2: pin 3
  //   Q_A: pin 8
endmodule
