// Digital circuit 74697.dig as structural Verilog
module _74697 (
  input  CCK,
  input  nENT,
  input  nENP,
  input  nLOAD,
  input  U_nD,
  input  nCCLR,
  input  RCK,
  input  R_nC,
  input  nG,
  input  A,
  input  B,
  input  C,
  input  D,
  input  VCC,
  input  GND,
  output Qa,
  output Qb,
  output Qc,
  output Qd,
  output nRCO
);

  wire and_1_out, and_2_out, and_3_out, and_4_out, and_5_out, and_6_out, and_7_out, and_8_out, and_9_out,
       and_10_out, and_11_out, and_12_out, and_13_out, and_14_out, and_15_out, and_16_out, and_17_out,
       and_18_out, and_19_out, and_20_out, and_21_out, and_22_out, and_23_out, and_24_out, and_25_out,
       d_ff_1_nq, d_ff_2_nq, d_ff_3_nq, d_ff_4_nq, d_ff_as_1_nq, d_ff_as_1_q, d_ff_as_2_nq, d_ff_as_2_q,
       d_ff_as_3_nq, d_ff_as_3_q, d_ff_as_4_nq, d_ff_as_4_q, nor_1_out, nor_2_out, nor_3_out, nor_4_out,
       nor_5_out, nor_6_out, nor_7_out, nor_8_out, nor_9_out, nor_10_out, nor_11_out, nor_12_out, nor_13_out,
       nor_14_out, nor_15_out, nor_16_out, not_1_out, not_2_out, not_3_out, not_4_out, not_5_out, not_6_out,
       not_7_out, not_8_out, not_9_out, not_10_out, not_11_out, not_12_out, not_13_out, not_14_out,
       not_15_out, not_16_out, not_17_out, not_18_out, not_19_out, not_20_out, or_1_out, or_2_out, or_3_out;

  not not_1 (not_1_out, R_nC);
  not not_2 (not_2_out, RCK);
  not not_3 (not_3_out, nCCLR);
  not not_4 (not_4_out, U_nD);
  not not_5 (not_5_out, nLOAD);
  not not_6 (not_6_out, CCK);
  nor nor_1 (nor_1_out, not_10_out, A);
  nor nor_2 (nor_2_out, not_10_out, B);
  nor nor_3 (nor_3_out, not_10_out, C);
  nor nor_4 (nor_4_out, not_10_out, D);
  PullUp pullup_1 (.out(VCC));
  PullDown pulldown_1 (.out(GND));
  not not_7 (not_7_out, not_1_out);
  not not_8 (not_8_out, not_3_out);
  not not_9 (not_9_out, not_4_out);
  not not_10 (not_10_out, not_5_out);
  and and_1 (and_1_out, ~not_5_out, ~nENP, ~nENT);  // And
  not not_11 (not_11_out, nENT);
  and and_2 (and_2_out, d_ff_as_1_q, not_4_out);
  and and_3 (and_3_out, not_9_out, d_ff_as_1_nq);
  and and_4 (and_4_out, d_ff_as_2_q, not_4_out);
  and and_5 (and_5_out, not_9_out, d_ff_as_2_nq);
  and and_6 (and_6_out, d_ff_as_3_q, not_4_out);
  and and_7 (and_7_out, not_9_out, d_ff_as_3_nq);
  and and_8 (and_8_out, d_ff_as_4_q, not_4_out);
  and and_9 (and_9_out, not_9_out, d_ff_as_4_nq);
  nor nor_5 (nor_5_out, and_2_out, and_3_out);
  nor nor_6 (nor_6_out, and_4_out, and_5_out);
  nor nor_7 (nor_7_out, and_6_out, and_7_out);
  nor nor_8 (nor_8_out, and_8_out, and_9_out);
  not not_12 (not_12_out, and_1_out);
  or or_1 (or_1_out, ~and_1_out, ~nor_5_out);  // Or
  or or_2 (or_2_out, ~and_1_out, ~nor_5_out, ~nor_6_out);  // Or
  or or_3 (or_3_out, ~and_1_out, ~nor_5_out, ~nor_6_out, ~nor_7_out);  // Or
  and and_10 (and_10_out, d_ff_as_1_q, and_1_out);
  and and_11 (and_11_out, not_12_out, not_10_out, d_ff_as_1_nq);
  nor nor_9 (nor_9_out, and_10_out, and_11_out, nor_1_out);
  nand nand_1 (nRCO, nor_5_out, nor_6_out, nor_7_out, nor_8_out, not_11_out);
  and and_12 (and_12_out, d_ff_as_2_q, and_1_out, nor_5_out);
  and and_13 (and_13_out, or_1_out, not_10_out, d_ff_as_2_nq);
  and and_14 (and_14_out, d_ff_as_3_q, and_1_out, nor_5_out, nor_6_out);
  and and_15 (and_15_out, or_2_out, not_10_out, d_ff_as_3_nq);
  and and_16 (and_16_out, d_ff_as_4_q, and_1_out, nor_5_out, nor_6_out, nor_7_out);
  and and_17 (and_17_out, or_3_out, not_10_out, d_ff_as_4_nq);
  nor nor_10 (nor_10_out, and_16_out, and_17_out, nor_4_out);
  nor nor_11 (nor_11_out, and_12_out, and_13_out, nor_2_out);
  nor nor_12 (nor_12_out, and_14_out, and_15_out, nor_3_out);
  not not_13 (not_13_out, not_6_out);
  not not_14 (not_14_out, not_8_out);
  not not_15 (not_15_out, not_6_out);
  not not_16 (not_16_out, not_8_out);
  not not_17 (not_17_out, not_6_out);
  not not_18 (not_18_out, not_8_out);
  not not_19 (not_19_out, not_6_out);
  not not_20 (not_20_out, not_8_out);
  D_FF_AS d_ff_as_1 (.Set(1'b0), .D(nor_9_out), .C(not_13_out), .Clr(not_14_out), .Q(d_ff_as_1_q), .nQ(d_ff_as_1_nq));
  D_FF_AS d_ff_as_2 (.Set(1'b0), .D(nor_11_out), .C(not_15_out), .Clr(not_16_out), .Q(d_ff_as_2_q), .nQ(d_ff_as_2_nq));
  D_FF_AS d_ff_as_3 (.Set(1'b0), .D(nor_12_out), .C(not_17_out), .Clr(not_18_out), .Q(d_ff_as_3_q), .nQ(d_ff_as_3_nq));
  D_FF_AS d_ff_as_4 (.Set(1'b0), .D(nor_10_out), .C(not_19_out), .Clr(not_20_out), .Q(d_ff_as_4_q), .nQ(d_ff_as_4_nq));
  D_FF d_ff_1 (.D(d_ff_as_1_q), .C(not_2_out), .nQ(d_ff_1_nq));  // open: Q
  D_FF d_ff_2 (.D(d_ff_as_2_q), .C(not_2_out), .nQ(d_ff_2_nq));  // open: Q
  D_FF d_ff_3 (.D(d_ff_as_3_q), .C(not_2_out), .nQ(d_ff_3_nq));  // open: Q
  D_FF d_ff_4 (.D(d_ff_as_4_q), .C(not_2_out), .nQ(d_ff_4_nq));  // open: Q
  and and_18 (and_18_out, not_7_out, d_ff_1_nq);
  and and_19 (and_19_out, not_1_out, d_ff_as_1_nq);
  and and_20 (and_20_out, not_7_out, d_ff_2_nq);
  and and_21 (and_21_out, not_1_out, d_ff_as_2_nq);
  and and_22 (and_22_out, not_7_out, d_ff_3_nq);
  and and_23 (and_23_out, not_1_out, d_ff_as_3_nq);
  and and_24 (and_24_out, not_7_out, d_ff_4_nq);
  and and_25 (and_25_out, not_1_out, d_ff_as_4_nq);
  nor nor_13 (nor_13_out, and_18_out, and_19_out);
  nor nor_14 (nor_14_out, and_20_out, and_21_out);
  nor nor_15 (nor_15_out, and_22_out, and_23_out);
  nor nor_16 (nor_16_out, and_24_out, and_25_out);
  assign Qa = ~nG ? nor_13_out : 1'bz;  // DriverInvSel driverinvsel_1
  assign Qb = ~nG ? nor_14_out : 1'bz;  // DriverInvSel driverinvsel_2
  assign Qc = ~nG ? nor_15_out : 1'bz;  // DriverInvSel driverinvsel_3
  assign Qd = ~nG ? nor_16_out : 1'bz;  // DriverInvSel driverinvsel_4

  // Notes on the sheet:
  //   CCK: pin 2
  //   nENT: pin 14
  //   nENP: pin 7
  //   nLOAD: pin 13, default 1
  //   U_nD: pin 1
  //   nCCLR: pin 8, default 1
  //   RCK: pin 9
  //   R_nC: pin 11
  //   nG: pin 12, default 1
  //   A: pin 3
  //   B: pin 4
  //   C: pin 5
  //   D: pin 6
  //   Qa: pin 18
  //   Qb: pin 17
  //   Qc: pin 16
  //   Qd: pin 15
  //   nRCO: pin 19
  //   VCC: pin 20
  //   GND: pin 10
endmodule
