// Digital circuit 74779-duplicate.dig as structural Verilog
module _74779_duplicate (
  input  CP,
  input  S0,
  input  S1,
  input  nOE,
  input  nCET,
  output nTC,
  output I_O7,
  output I_O6,
  output I_O5,
  output I_O4,
  output I_O3,
  output I_O2,
  output I_O1,
  output I_O0
);

  wire _74269_detail_1_nq, _74269_detail_1_q, _74269_detail_2_nq, _74269_detail_2_q, _74269_detail_3_nq,
       _74269_detail_3_q, _74269_detail_4_nq, _74269_detail_4_q, _74269_detail_5_nq, _74269_detail_5_q,
       _74269_detail_6_nq, _74269_detail_6_q, _74269_detail_7_nq, _74269_detail_7_q, _74269_detail_8_nq,
       _74269_detail_8_q, and_1_out, and_2_out, and_3_out, and_4_out, and_5_out, and_6_out, and_7_out,
       and_8_out, and_9_out, and_10_out, and_11_out, and_12_out, and_13_out, and_14_out, and_15_out,
       and_16_out, and_17_out, and_18_out, and_19_out, and_20_out, and_21_out, nor_2_out, nor_3_out,
       nor_4_out, nor_5_out, nor_6_out, nor_7_out, nor_8_out, nor_9_out, not_1_out, not_2_out, not_3_out,
       not_4_out, not_5_out, not_6_out, not_7_out, not_8_out, not_9_out, not_10_out, not_11_out;

  not not_1 (not_1_out, S0);
  not not_2 (not_2_out, S1);
  and and_1 (and_1_out, not_1_out, not_2_out);
  and and_2 (and_2_out, ~not_2_out, not_1_out);  // And
  and and_3 (and_3_out, not_2_out, ~not_1_out);  // And
  assign I_O0 = ~nOE ? not_4_out : 1'bz;  // DriverInvSel driverinvsel_1
  assign I_O1 = ~nOE ? not_5_out : 1'bz;  // DriverInvSel driverinvsel_2
  assign I_O2 = ~nOE ? not_6_out : 1'bz;  // DriverInvSel driverinvsel_3
  assign I_O3 = ~nOE ? not_7_out : 1'bz;  // DriverInvSel driverinvsel_4
  assign I_O4 = ~nOE ? not_8_out : 1'bz;  // DriverInvSel driverinvsel_5
  assign I_O5 = ~nOE ? not_9_out : 1'bz;  // DriverInvSel driverinvsel_6
  assign I_O6 = ~nOE ? not_10_out : 1'bz;  // DriverInvSel driverinvsel_7
  assign I_O7 = ~nOE ? not_11_out : 1'bz;  // DriverInvSel driverinvsel_8
  not not_3 (not_3_out, nCET);
  not not_4 (not_4_out, _74269_detail_1_nq);
  not not_5 (not_5_out, _74269_detail_2_nq);
  not not_6 (not_6_out, _74269_detail_3_nq);
  not not_7 (not_7_out, _74269_detail_4_nq);
  not not_8 (not_8_out, _74269_detail_5_nq);
  not not_9 (not_9_out, _74269_detail_6_nq);
  not not_10 (not_10_out, _74269_detail_7_nq);
  not not_11 (not_11_out, _74269_detail_8_nq);
  nor nor_1 (nTC, and_13_out, and_4_out);
  and and_4 (and_4_out, _74269_detail_8_nq, not_3_out, not_3_out, not_3_out, not_3_out, not_3_out, not_3_out, _74269_detail_1_nq, and_3_out, not_3_out);
  and and_5 (and_5_out, and_3_out, not_3_out);
  and and_6 (and_6_out, _74269_detail_1_nq, and_3_out, not_3_out);
  and and_7 (and_7_out, not_3_out, _74269_detail_1_nq, and_3_out, not_3_out);
  and and_8 (and_8_out, not_3_out, not_3_out, _74269_detail_1_nq, and_3_out, not_3_out);
  and and_9 (and_9_out, not_3_out, not_3_out, not_3_out, _74269_detail_1_nq, and_3_out, not_3_out);
  and and_10 (and_10_out, not_3_out, not_3_out, not_3_out, not_3_out, _74269_detail_1_nq, and_3_out, not_3_out);
  and and_11 (and_11_out, not_3_out, not_3_out, not_3_out, not_3_out, not_3_out, _74269_detail_1_nq, and_3_out, not_3_out);
  and and_12 (and_12_out, not_3_out, not_3_out, not_3_out, not_3_out, not_3_out, not_3_out, _74269_detail_1_nq, and_3_out, not_3_out);
  and and_13 (and_13_out, _74269_detail_8_q, _74269_detail_7_q, _74269_detail_6_q, _74269_detail_5_q, _74269_detail_4_q, _74269_detail_3_q, _74269_detail_2_q, _74269_detail_1_q, and_2_out, not_3_out);
  and and_14 (and_14_out, not_3_out, and_2_out);
  and and_15 (and_15_out, not_3_out, _74269_detail_1_q, and_2_out);
  and and_16 (and_16_out, not_3_out, _74269_detail_2_q, _74269_detail_1_q, and_2_out);
  and and_17 (and_17_out, not_3_out, _74269_detail_3_q, _74269_detail_2_q, _74269_detail_1_q, and_2_out);
  and and_18 (and_18_out, not_3_out, _74269_detail_4_q, _74269_detail_3_q, _74269_detail_2_q, _74269_detail_1_q, and_2_out);
  and and_19 (and_19_out, not_3_out, _74269_detail_5_q, _74269_detail_4_q, _74269_detail_3_q, _74269_detail_2_q, _74269_detail_1_q, and_2_out);
  and and_20 (and_20_out, not_3_out, _74269_detail_6_q, _74269_detail_5_q, _74269_detail_4_q, _74269_detail_3_q, _74269_detail_2_q, _74269_detail_1_q, and_2_out);
  and and_21 (and_21_out, not_3_out, _74269_detail_7_q, _74269_detail_6_q, _74269_detail_5_q, _74269_detail_4_q, _74269_detail_3_q, _74269_detail_2_q, _74269_detail_1_q, and_2_out);
  nor nor_2 (nor_2_out, and_14_out, and_5_out);
  nor nor_3 (nor_3_out, and_15_out, and_6_out);
  nor nor_4 (nor_4_out, and_16_out, and_7_out);
  nor nor_5 (nor_5_out, and_17_out, and_8_out);
  nor nor_6 (nor_6_out, and_18_out, and_9_out);
  nor nor_7 (nor_7_out, and_19_out, and_10_out);
  nor nor_8 (nor_8_out, and_20_out, and_11_out);
  nor nor_9 (nor_9_out, and_21_out, and_12_out);
  _74269_detail _74269_detail_1 (
    .Dn(I_O0), .PE(and_1_out), .nTOGGLE(nor_2_out), .nCP(CP), .Q(_74269_detail_1_q), .nQ(_74269_detail_1_nq));
  _74269_detail _74269_detail_2 (
    .Dn(I_O1), .PE(and_1_out), .nTOGGLE(nor_3_out), .nCP(CP), .Q(_74269_detail_2_q), .nQ(_74269_detail_2_nq));
  _74269_detail _74269_detail_3 (
    .Dn(I_O2), .PE(and_1_out), .nTOGGLE(nor_4_out), .nCP(CP), .Q(_74269_detail_3_q), .nQ(_74269_detail_3_nq));
  _74269_detail _74269_detail_4 (
    .Dn(I_O3), .PE(and_1_out), .nTOGGLE(nor_5_out), .nCP(CP), .Q(_74269_detail_4_q), .nQ(_74269_detail_4_nq));
  _74269_detail _74269_detail_5 (
    .Dn(I_O4), .PE(and_1_out), .nTOGGLE(nor_6_out), .nCP(CP), .Q(_74269_detail_5_q), .nQ(_74269_detail_5_nq));
  _74269_detail _74269_detail_6 (
    .Dn(I_O5), .PE(and_1_out), .nTOGGLE(nor_7_out), .nCP(CP), .Q(_74269_detail_6_q), .nQ(_74269_detail_6_nq));
  _74269_detail _74269_detail_7 (
    .Dn(I_O6), .PE(and_1_out), .nTOGGLE(nor_8_out), .nCP(CP), .Q(_74269_detail_7_q), .nQ(_74269_detail_7_nq));
  _74269_detail _74269_detail_8 (
    .Dn(I_O7), .PE(and_1_out), .nTOGGLE(nor_9_out), .nCP(CP), .Q(_74269_detail_8_q), .nQ(_74269_detail_8_nq));

  // Notes on the sheet:
  //   CP: default 15
  //   S0: default 15
  //   S1: default 15
  //   https://pdf1.alldatasheet.com/datasheet-pdf/view/15487/PHILIPS/74F779.html
endmodule
