// Digital circuit tom-1-245.dig as structural Verilog
module tom_1_245 (
  input  [7:0] \input ,
  input  noe,
  input  DIR,
  output [7:0] out
);

  _74245 _74245_1 (
    .pin1(DIR), .pin2(\input [0]), .pin3(\input [1]), .pin4(\input [2]), .pin5(\input [3]),
    .pin6(\input [4]), .pin7(\input [5]), .pin8(\input [6]), .pin9(\input [7]), .pin10(1'b0), .pin11(out[7]),
    .pin12(out[6]), .pin13(out[5]), .pin14(out[4]), .pin15(out[3]), .pin16(out[2]), .pin17(out[1]),
    .pin18(out[0]), .pin19(noe), .pin20(1'b1));
endmodule
