// Digital circuit tom-1-273.dig as structural Verilog
module tom_1_273 (
  input  nCLR,
  input  [7:0] DATA,
  input  CLK,
  output [7:0] OUT
);

  _74273 _74273_1 (
    .pin1(nCLR), .pin2(OUT[7]), .pin3(DATA[7]), .pin4(DATA[6]), .pin5(OUT[6]), .pin6(OUT[5]), .pin7(DATA[5]),
    .pin8(DATA[4]), .pin9(OUT[4]), .pin10(1'b0), .pin11(CLK), .pin12(OUT[3]), .pin13(DATA[3]),
    .pin14(DATA[2]), .pin15(OUT[2]), .pin16(OUT[1]), .pin17(DATA[1]), .pin18(DATA[0]), .pin19(OUT[0]),
    .pin20(1'b1));
endmodule
