// Digital circuit tom-1-add.dig as structural Verilog
module tom_1_add (
  input  [15:0] A,
  input  [15:0] B,
  input  enable,
  output [15:0] out
);

  wire tom_1_283_1_c4, tom_1_283_2_c4, tom_1_283_3_c4;
  wire [3:0] tom_1_283_1_s, tom_1_283_2_s, tom_1_283_3_s, tom_1_283_4_s;

  tom_1_283 tom_1_283_1 (.C0(1'b0), .A(A[3:0]), .B(B[3:0]), .C4(tom_1_283_1_c4), .S(tom_1_283_1_s));
  tom_1_283 tom_1_283_2 (.C0(tom_1_283_1_c4), .A(A[7:4]), .B(B[7:4]), .C4(tom_1_283_2_c4), .S(tom_1_283_2_s));
  tom_1_283 tom_1_283_3 (.C0(tom_1_283_2_c4), .A(A[11:8]), .B(B[11:8]), .C4(tom_1_283_3_c4), .S(tom_1_283_3_s));
  tom_1_283 tom_1_283_4 (.C0(tom_1_283_3_c4), .A(A[15:12]), .B(B[15:12]), .S(tom_1_283_4_s));  // open: C4
  assign out = enable ? {tom_1_283_4_s, tom_1_283_3_s, tom_1_283_2_s, tom_1_283_1_s} : 16'bz;  // Driver driver_1
  // Pins of 1 and 16 bits meet at A
  // Pins of 1 and 16 bits meet at B
endmodule
