// Digital circuit tom-1-is0.dig as structural Verilog
module tom_1_is0 (
  input  [15:0] \input ,
  output nis0
);

  or or_1 (nis0, \input [0], \input [1], \input [2], \input [3], \input [4], \input [5], \input [6], \input [7], \input [8], \input [9], \input [10], \input [11], \input [12], \input [13], \input [14], \input [15]);
endmodule
