// Digital circuit tom-1-rom.dig as structural Verilog
module tom_1_rom (
  input  [7:0] address,
  input  A,
  output [15:0] data
);

  // _28c16 _28c16_1: pin names not known; wires that end beside it: address[7], address[6], address[5], address[4], address[3], address[2], address[1], address[0], data[0], data[1], data[2], 1'b0, 1'b1, 1'b0, 1'b0, 1'b1, 1'b0, 1'b0, 1'b0, data[7], data[6], data[5]
  // _28c16 _28c16_2: pin names not known; wires that end beside it: address[7], address[6], address[5], address[4], address[3], address[2], address[1], address[0], data[8], data[9], data[10], 1'b0, 1'b1, 1'b0, 1'b0, 1'b1, 1'b0, 1'b0, 1'b0, data[15], data[14], data[13]
  SixteenSeg sixteenseg_1 (.led(data), .dp(A));
endmodule
