// Digital circuit tom-1.dig as structural Verilog
module tom_1 (
  input  clk,
  input  in_2,
  output clk_2,
  output clk_not,
  output [15:0] pc,
  output [15:0] stack_bus,
  output [15:0] tos,
  output [7:0] dr,
  output dr_cck,
  output [8:0] stack_addr,
  output [15:0] tos_bus,
  output [15:0] operand,
  output phase,
  output [7:0] ctrl,
  output io_clk,
  output [7:0] io_data
);

  wire d_ff_1_q, d_ff_2_q, delay_1_out, delay_3_out, driver_1_out, not_1_out, not_2_out, not_3_out,
       not_4_out, not_5_out, not_6_out, not_7_out, not_8_out, nTOS_eq__eq_0_nis0, or_1_out, or_2_out,
       or_3_out, or_4_out, or_5_out, PC__LO_ntc;
  wire [3:0] tom_139_1__1c, tom_139_1__2c;
  wire [15:0] delay_4_out;

  assign driver_1_out = in_2 ? clk_2 : 1'bz;  // Driver driver_1
  Break break_1 (.brk(driver_1_out));
  tom_1_is0 nTOS_eq__eq_0 (.\input (tos), .nis0(nTOS_eq__eq_0_nis0));
  SixteenSeg sixteenseg_1 (.led(tos), .dp(1'b0));
  D_FF d_ff_1 (.D(delay_1_out), .C(pc[0]), .Q(d_ff_1_q));  // open: nQ
  Delay #(.delayTime(10)) delay_1 (.in(nTOS_eq__eq_0_nis0), .out(delay_1_out));
  LED led_1 (.in(ctrl[0]));
  LED led_2 (.in(ctrl[1]));
  LED led_3 (.in(ctrl[2]));
  LED led_4 (.in(ctrl[3]));
  LED led_5 (.in(ctrl[4]));
  LED led_6 (.in(ctrl[5]));
  LED led_7 (.in(ctrl[6]));
  LED led_8 (.in(ctrl[7]));
  or or_1 (or_1_out, d_ff_1_q, tom_139_1__2c[2]);
  not not_1 (not_1_out, ctrl[3]);
  not not_2 (not_2_out, or_1_out);
  not not_3 (not_3_out, ctrl[1]);
  not not_4 (not_4_out, ctrl[2]);
  tom_139 tom_139_1 (
    ._1A(ctrl[4]), ._1B(ctrl[5]), ._2A(ctrl[6]), ._2B(ctrl[7]), ._1C(tom_139_1__1c), ._2C(tom_139_1__2c));
  D_FF d_ff_2 (.D(operand[0]), .C(not_2_out), .Q(d_ff_2_q));  // open: nQ
  not not_5 (not_5_out, pc[0]);
  or or_2 (or_2_out, ctrl[1], not_1_out);
  or or_3 (or_3_out, not_3_out, not_1_out);
  LED HALT (.in(d_ff_2_q));
  tom_269 PC__LO (
    .nPE(or_1_out), .U_nD(1'b1), .CP(clk_2), .nCEP(d_ff_2_q), .nCET(1'b0), .D({operand[7:1], 1'b0}),
    .Q(pc[7:0]), .nTC(PC__LO_ntc));
  tom_269 PC__HI (
    .nPE(or_1_out), .U_nD(1'b1), .CP(clk_2), .nCEP(PC__LO_ntc), .nCET(1'b0), .D(operand[15:8]), .Q(pc[15:8]));  // open: nTC
  // tom_374 TOS__LO: pin names not known; wires that end beside it: tos_bus[7:0], ctrl[0], not_5_out, tos[7:0]
  // tom_374 TOS__HI: pin names not known; wires that end beside it: tos_bus[15:8], ctrl[0], not_5_out, tos[15:8]
  tom_779 D (.nOE(ctrl[1]), .nCET(or_2_out), .CP(clk_not), .S0(not_4_out), .S1(ctrl[2]), .I_O(dr));  // open: nTC
  tom_779 R (.nOE(or_3_out), .nCET(not_3_out), .CP(clk_not), .S0(not_4_out), .S1(ctrl[2]), .I_O(dr));  // open: nTC
  Delay delay_2 (.in(ctrl[1]), .out(stack_addr[8]));
  not not_6 (not_6_out, ctrl[4]);
  Delay #(.delayTime(3)) delay_3 (.in(ctrl[4]), .out(delay_3_out));
  not not_7 (not_7_out, tom_139_1__2c[1]);
  EEPROM #(.AddrBits(16), .isProgramMemory("true"), .Bits(16)) ROM (
    .A(pc), .CS(1'b1), .WE(1'b0), .OE(1'b1), .D({ctrl, operand[7:0]}));
  Delay #(.Bits(16)) delay_4 (.in(tos), .out(delay_4_out));
  or or_4 (or_4_out, clk_2, delay_3_out);
  or or_5 (or_5_out, clk_2, not_6_out);
  // tom_1_373 T2SB__LO: pin names not known; wires that end beside it: tos[7:0], tom_139_1__1c[3], 1'b1, stack_bus[7:0]
  // tom_1_373 T2SB__HI: pin names not known; wires that end beside it: tos[15:8], tom_139_1__1c[3], 1'b1, stack_bus[15:8]
  // tom_374 ROM_BUFFER: pin names not known; wires that end beside it: operand[7:0], 1'b0, pc[0], operand[15:8]
  RAMSinglePortSel #(.AddrBits(16), .Bits(16)) RAM (
    .A(delay_4_out), .CS(~ctrl[5]), .WE(~or_4_out), .OE(~not_6_out), .D(stack_bus));
  RAMSinglePortSel #(.AddrBits(9), .Bits(16)) STACK (
    .A({stack_addr[8], dr}), .CS(~1'b0), .WE(~or_5_out), .OE(~delay_3_out), .D(stack_bus));
  not not_8 (not_8_out, ctrl[5]);
  nand nand_1 (io_clk, not_8_out, clk_not, not_7_out);
  D_FF d_ff_3 (.D(clk_not), .C(clk), .Q(clk_2), .nQ(clk_not));
  // tom_1_373 R2TB__LO: pin names not known; wires that end beside it: operand[7:0], tom_139_1__2c[0], 1'b1, tos_bus[7:0]
  // tom_1_373 R2TB__HI: pin names not known; wires that end beside it: operand[15:8], tom_139_1__2c[0], 1'b1, tos_bus[15:8]
  // tom_1_add ADD: pin names not known; wires that end beside it: tos, stack_bus, ctrl[7], tos_bus
  tom_1_nand NAND_2 (.A(tos), .B(stack_bus), .enable(not_7_out), .out(tos_bus));
  tom_1_245 tom_1_245_1 (.\input (stack_bus[7:0]), .noe(io_clk), .DIR(or_4_out), .out(io_data));
  tom_io tom_io_1 (.clk(io_clk), .data(io_data));

  assign dr_cck = clk_not;
  assign phase = pc[0];
  assign stack_addr[7:0] = dr;

  // Other names for the same wires on the sheet: clk_t = clk_2; nclk = clk_not

  // Notes on the sheet:
  //   clk: Hz: 1000
  //   in_2: default 1
  //   Program
  //   BRANCH0 ^
  //   Process
  //   CTRL
  //   0=STACK 1=STORE 2=RAM 3=TOS
  //   ^ ROM_en
  //   TOMSCII
  //   ^ TOS
  //   TOS-DISABLE
  //   DR-SEL
  //   DR-UP
  //   DR-CCK
  //   CPU-BUS-SEL-1
  //   CPU-BUS-SEL-2
  //   TOS-BUS-SEL-1
  //   TOS-BUS-SEL-2
  //   PHASE
  //   contents of ROM (hex, n*v repeats v):
  //   2000,2100,3c00,3002,3c00,3018,800,e900,3c00,3027,3c00,3016,800,e900,3c00,3001,3c00,
  //   3000,800,e900,3c00,3000,3c01,3000,800,e900,3c00,3000,3c00,3018,800,e900,3c00,3000,
  //   3c00,3016,800,e900,3c00,3004,3c00,3017,800,e900,3c00,3000,3c00,3014,800,e900,3c00,
  //   3016,1c00,e900,3c00,3015,800,e900,3c00,3015,1c00,e900,3c00,3014,1c00,e900,2800,e000,
  //   3c00,e100,3c00,3008,800,e900,3c00,30ff,2800,6000,3cff,30ff,2800,6000,3c00,3015,800,
  //   e900,3c00,3015,5c00,e900,3c00,3017,5c00,e900,3c00,3014,1c00,e900,3c00,30ff,3cff,30ff,
  //   2800,6000,3c00,3001,2800,e000,2800,e000,3c00,e100,3c00,3008,800,e900,3c00,30ff,2800,
  //   6000,3cff,30ff,2800,6000,3c00,3014,800,e900,3c00,3014,1c00,e900,3c00,3008,3cff,30ff,
  //   2800,6000,3c00,3001,2800,e000,2800,e000,3c00,3008,800,e900,3c00,3008,1c00,e900,3c00,
  //   30ff,2800,6000,3cff,30ff,2800,6000,2800,a1a6,3c00,3000,2800,a132,3c00,3016,1c00,e900,
  //   3c00,30f8,3cff,30ff,2800,6000,3c00,3001,2800,e000,2800,e000,3c00,e100,3c00,3008,800,
  //   e900,3c00,30ff,2800,6000,3cff,30ff,2800,6000,3c00,3016,800,e900,3c00,3018,1c00,e900,
  //   3c00,30ff,3cff,30ff,2800,6000,3c00,3001,2800,e000,2800,e000,3c00,e100,3c00,3008,800,
  //   e900,3c00,30ff,2800,6000,3cff,30ff,2800,6000,3c00,3018,800,e900,3c00,3018,1c00,e900,
  //   3c00,3008,3cff,30ff,2800,6000,3c00,3001,2800,e000,2800,e000,3c00,3008,800,e900,3c00,
  //   3008,1c00,e900,3c00,30ff,2800,6000,3cff,30ff,2800,6000,2801,a110,3c00,3000,2800,a12c,
  //   3c00,3000,3c00,3014,800,e900,3c00,3006,3c00,3015,800,e900,3c00,3014,5c00,e900,3c00,
  //   3015,5c00,e900,3c00,3038,3c00,3016,800,e900,3c00,3016,1c00,e900,3c00,3014,1c00,e900,
  //   2800,e000,3c00,e100,3c00,3008,800,e900,3c00,30ff,2800,6000,3cff,30ff,2800,6000,3c00,
  //   3016,800,e900,3c00,3016,5c00,e900,3c00,3015,5c00,e900,3c00,3014,1c00,e900,3c00,30ff,
  //   3cff,30ff,2800,6000,3c00,3001,2800,e000,2800,e000,3c00,e100,3c00,3008,800,e900,3c00,
  //   30ff,2800,6000,3cff,30ff,2800,6000,3c00,3014,800,e900,3c00,3014,1c00,e900,3c00,3008,
  //   3cff,30ff,2800,6000,3c00,3001,2800,e000,2800,e000,3c00,3008,800,e900,3c00,3008,1c00,
  //   e900,3c00,30ff,2800,6000,3cff,30ff,2800,6000,2801,a196,3c00,3000,2801,a11c,3c00,3000,
  //   3c00,3014,800,e900,3c00,3006,3c00,3015,800,e900,3c00,3014,5c00,e900,3c00,3015,5c00,
  //   e900,3c00,3007,3c00,3016,800,e900,3c00,3016,1c00,e900,3c00,3014,1c00,e900,2800,e000,
  //   3c00,e100,3c00,3008,800,e900,3c00,30ff,2800,6000,3cff,30ff,2800,6000,3c00,3016,800,
  //   e900,3c00,3016,5c00,e900,3c00,3015,5c00,e900,3c00,3014,1c00,e900,3c00,30f8,3cff,30ff,
  //   2800,6000,3c00,3001,2800,e000,2800,e000,3c00,e100,3c00,3008,800,e900,3c00,30ff,2800,
  //   6000,3cff,30ff,2800,6000,3c00,3014,800,e900,3c00,3014,1c00,e900,3c00,3040,3cff,30ff,
  //   2800,6000,3c00,3001,2800,e000,2800,e000,3c00,3008,800,e900,3c00,3008,1c00,e900,3c00,
  //   30ff,2800,6000,3cff,30ff,2800,6000,2802,a11c,3c00,3000,2801,a1a2,3c00,3000,3c00,3018,
  //   800,e900,3c00,3018,1c00,e900,3c00,e900
  //   v CTRL
  //   PHASE v
  //   8-BIT TRUNCATE
  //   TOS_bus v
  //   Spare D Flip Flop
endmodule
