// Digital circuit tom-269.dig as structural Verilog
module tom_269 (
  input  nPE,
  input  U_nD,
  input  CP,
  input  nCEP,
  input  nCET,
  input  [7:0] D,
  output [7:0] Q,
  output nTC
);

  _74269 _74269_1 (
    .D0(D[0]), .D1(D[1]), .D2(D[2]), .D4(D[4]), .D3(D[3]), .D5(D[5]), .D6(D[6]), .D7(D[7]), .nPE(nPE),
    .CP(CP), .U_nD(U_nD), .nCEP(nCEP), .nCET(nCET), .nTC(nTC), .Q7(Q[7]), .Q6(Q[6]), .Q5(Q[5]), .Q4(Q[4]),
    .Q3(Q[3]), .Q2(Q[2]), .Q1(Q[1]), .Q0(Q[0]));
endmodule
