// Digital circuit tom-299.dig as structural Verilog
module tom_299 (
  input  SL,
  input  S0,
  input  S1,
  input  nG1,
  input  nG2,
  input  nCLR,
  input  CLK,
  input  SR,
  input  [7:0] DATA,
  output Q_A,
  output Q_H
);

  wire and_1_out, bussplitter_1_d0, bussplitter_1_d1, bussplitter_1_d2, bussplitter_1_d3, bussplitter_1_d4,
       bussplitter_1_d5, bussplitter_1_d6, bussplitter_1_d7;

  and and_1 (and_1_out, S0, S1);
  BusSplitter #(.Bits(8)) bussplitter_1 (
    .D(DATA), .OE(and_1_out), .D0(bussplitter_1_d0), .D1(bussplitter_1_d1), .D2(bussplitter_1_d2),
    .D3(bussplitter_1_d3), .D4(bussplitter_1_d4), .D5(bussplitter_1_d5), .D6(bussplitter_1_d6),
    .D7(bussplitter_1_d7));
  _74299 _74299_1 (
    .A_Q_A(bussplitter_1_d0), .B_Q_B(bussplitter_1_d1), .C_Q_C(bussplitter_1_d2), .D_Q_D(bussplitter_1_d3),
    .E_Q_E(bussplitter_1_d4), .F_Q_F(bussplitter_1_d5), .G_Q_G(bussplitter_1_d6), .H_Q_H(bussplitter_1_d7),
    .Q_H(Q_H), .SLSI(SL), .S0(S0), .S1(S1), .nCLK(CLK), .SRSI(SR), .CLR(nCLR), .nG1(nG1), .nG2(nG2), .Q_A(Q_A));
endmodule
