// Digital circuit tom-779.dig as structural Verilog
module tom_779 (
  input  nOE,
  input  nCET,
  input  CP,
  input  S0,
  input  S1,
  output [7:0] I_O,
  output nTC
);

  _74779 _74779_1 (
    .pin1(I_O[1]), .pin2(I_O[2]), .pin3(I_O[3]), .pin4(1'b0), .pin5(I_O[4]), .pin6(I_O[5]), .pin7(I_O[6]),
    .pin8(I_O[7]), .pin9(nOE), .pin10(S1), .pin11(S0), .pin12(nTC), .pin13(1'b1), .pin14(nCET), .pin15(CP),
    .pin16(I_O[0]));
endmodule
