// Digital circuit tom-869.dig as structural Verilog
module tom_869 (
  input  nENP,
  input  S0,
  input  S1,
  input  [7:0] D,
  input  nENT,
  input  CLK,
  output [7:0] Q,
  output nRCO
);

  _74869 _74869_1 (
    .S0(S0), .S1(S1), .nENT(nENT), .nENP(nENP), .CLK(CLK), .A(D[0]), .H(D[7]), .G(D[6]), .F(D[5]), .E(D[4]),
    .D(D[3]), .C(D[2]), .B(D[1]), .Q_H(Q[7]), .Q_G(Q[6]), .Q_F(Q[5]), .Q_E(Q[4]), .Q_D(Q[3]), .Q_C(Q[2]),
    .Q_B(Q[1]), .Q_A(Q[0]), .nRCO(nRCO));
endmodule
