// Digital circuit tom-io.dig as structural Verilog
module tom_io (
  input  clk,
  input  [7:0] data
);

  wire and_1_out, d_ff_1_nq, d_ff_1_q, delay_1_out, delay_2_out;
  wire [7:0] register_1_q, register_2_q, register_3_q;

  Delay #(.delayTime(3)) delay_1 (.in(clk), .out(delay_1_out));
  Register #(.Bits(8)) register_1 (.D(data), .C(clk), .en(1'b1), .Q(register_1_q));
  D_FF d_ff_1 (.D(d_ff_1_nq), .C(delay_1_out), .Q(d_ff_1_q), .nQ(d_ff_1_nq));
  Delay #(.delayTime(2)) delay_2 (.in(delay_1_out), .out(delay_2_out));
  Register #(.Bits(8)) register_2 (.D(register_1_q), .C(delay_2_out), .en(d_ff_1_nq), .Q(register_2_q));
  Register #(.Bits(8)) register_3 (.D(register_1_q), .C(delay_2_out), .en(d_ff_1_q), .Q(register_3_q));
  Terminal terminal_1 (.D(register_1_q), .C(1'b0), .en(1'b1));
  GraphicCard #(.graphicHeight(8), .graphicWidth(8), .Bits(8)) graphiccard_1 (
    .A(register_2_q[6:0]), .str(d_ff_1_q), .C(and_1_out), .ld(1'b0), .B(1'b0), .D(register_3_q));
  and and_1 (and_1_out, d_ff_1_q, delay_2_out);
  // Probe on register_2_q[6:0]
  // Probe on register_3_q
endmodule
