// Digital circuit 74269-detail.dig as structural Verilog
module _74269_detail (
  input  Dn,
  input  PE,
  input  nTOGGLE,
  input  nCP,
  output Q,
  output nQ
);

  wire and_1_out, and_2_out, and_3_out, not_1_out, not_2_out, or_1_out;

  not not_1 (not_1_out, PE);
  not not_2 (not_2_out, nTOGGLE);
  and and_1 (and_1_out, Dn, PE);
  and and_2 (and_2_out, not_1_out, nTOGGLE, Q);
  and and_3 (and_3_out, not_1_out, not_2_out, nQ);
  or or_1 (or_1_out, and_1_out, and_2_out, and_3_out);
  D_FF d_ff_1 (.D(or_1_out), .C(~nCP), .Q(Q), .nQ(nQ));
endmodule
