// Digital circuit 74543.dig as structural Verilog
module _74543 (
  input  nOEBA,
  input  nCEBA,
  input  nLEBA,
  input  nOEAB,
  input  nCEAB,
  input  nLEAB,
  output B1,
  output A1,
  output B2,
  output A2,
  output B3,
  output A3,
  output B4,
  output A4,
  output B5,
  output A5,
  output B6,
  output A6,
  output B7,
  output A7,
  output B8,
  output A8
);

  wire and_1_out, and_2_out, and_3_out, and_4_out, d_ff_1_q, d_ff_2_q, d_ff_3_q, d_ff_4_q, d_ff_5_q,
       d_ff_6_q, d_ff_7_q, d_ff_8_q, d_ff_9_q, d_ff_10_q, d_ff_11_q, d_ff_12_q, d_ff_13_q, d_ff_14_q,
       d_ff_15_q, d_ff_16_q;

  and and_1 (and_1_out, ~nOEBA, ~nCEBA);  // And
  and and_2 (and_2_out, ~nCEBA, ~nLEBA);  // And
  and and_3 (and_3_out, ~nOEAB, ~nCEAB);  // And
  and and_4 (and_4_out, ~nCEAB, ~nLEAB);  // And
  D_FF d_ff_1 (.D(A1), .C(and_4_out), .Q(d_ff_1_q));  // open: nQ
  D_FF d_ff_2 (.D(A2), .C(and_4_out), .Q(d_ff_2_q));  // open: nQ
  D_FF d_ff_3 (.D(A3), .C(and_4_out), .Q(d_ff_3_q));  // open: nQ
  D_FF d_ff_4 (.D(A4), .C(and_4_out), .Q(d_ff_4_q));  // open: nQ
  D_FF d_ff_5 (.D(A5), .C(and_4_out), .Q(d_ff_5_q));  // open: nQ
  D_FF d_ff_6 (.D(A6), .C(and_4_out), .Q(d_ff_6_q));  // open: nQ
  D_FF d_ff_7 (.D(A7), .C(and_4_out), .Q(d_ff_7_q));  // open: nQ
  D_FF d_ff_8 (.D(A8), .C(and_4_out), .Q(d_ff_8_q));  // open: nQ
  assign A1 = and_1_out ? d_ff_9_q : 1'bz;  // Driver driver_1
  assign A2 = and_1_out ? d_ff_10_q : 1'bz;  // Driver driver_2
  assign A3 = and_1_out ? d_ff_11_q : 1'bz;  // Driver driver_3
  assign A4 = and_1_out ? d_ff_12_q : 1'bz;  // Driver driver_4
  assign A5 = and_1_out ? d_ff_13_q : 1'bz;  // Driver driver_5
  assign A6 = and_1_out ? d_ff_14_q : 1'bz;  // Driver driver_6
  assign A7 = and_1_out ? d_ff_15_q : 1'bz;  // Driver driver_7
  assign A8 = and_1_out ? d_ff_16_q : 1'bz;  // Driver driver_8
  D_FF d_ff_9 (.D(B1), .C(and_2_out), .Q(d_ff_9_q));  // open: nQ
  assign B1 = and_3_out ? d_ff_1_q : 1'bz;  // Driver driver_9
  D_FF d_ff_10 (.D(B2), .C(and_2_out), .Q(d_ff_10_q));  // open: nQ
  assign B2 = and_3_out ? d_ff_2_q : 1'bz;  // Driver driver_10
  D_FF d_ff_11 (.D(B3), .C(and_2_out), .Q(d_ff_11_q));  // open: nQ
  assign B3 = and_3_out ? d_ff_3_q : 1'bz;  // Driver driver_11
  D_FF d_ff_12 (.D(B4), .C(and_2_out), .Q(d_ff_12_q));  // open: nQ
  assign B4 = and_3_out ? d_ff_4_q : 1'bz;  // Driver driver_12
  D_FF d_ff_13 (.D(B5), .C(and_2_out), .Q(d_ff_13_q));  // open: nQ
  assign B5 = and_3_out ? d_ff_5_q : 1'bz;  // Driver driver_13
  D_FF d_ff_14 (.D(B6), .C(and_2_out), .Q(d_ff_14_q));  // open: nQ
  assign B6 = and_3_out ? d_ff_6_q : 1'bz;  // Driver driver_14
  D_FF d_ff_15 (.D(B7), .C(and_2_out), .Q(d_ff_15_q));  // open: nQ
  assign B7 = and_3_out ? d_ff_7_q : 1'bz;  // Driver driver_15
  D_FF d_ff_16 (.D(B8), .C(and_2_out), .Q(d_ff_16_q));  // open: nQ
  assign B8 = and_3_out ? d_ff_8_q : 1'bz;  // Driver driver_16

  // Notes on the sheet:
  //   B1: pin 22
  //   A1: pin 3
  //   B2: pin 21
  //   A2: pin 4
  //   B3: pin 20
  //   A3: pin 5
  //   B4: pin 19
  //   A4: pin 6
  //   B5: pin 18
  //   A5: pin 7
  //   B6: pin 17
  //   A6: pin 8
  //   B7: pin 16
  //   A7: pin 9
  //   B8: pin 15
  //   A8: pin 10
  //   nOEBA: pin 2
  //   nCEBA: pin 23
  //   nLEBA: pin 1
  //   nOEAB: pin 13
  //   nCEAB: pin 11
  //   nLEAB: pin 14
endmodule
