// Digital circuit 74869.dig as structural Verilog
module _74869 (
  input  S0,
  input  S1,
  input  nENT,
  input  nENP,
  input  CLK,
  input  A,
  input  H,
  input  G,
  input  F,
  input  E,
  input  D,
  input  C,
  input  B,
  output Q_H,
  output Q_G,
  output Q_F,
  output Q_E,
  output Q_D,
  output Q_C,
  output Q_B,
  output Q_A,
  output nRCO
);

  wire and_1_out, and_2_out, and_3_out, and_4_out, and_5_out, and_6_out, and_7_out, and_8_out, and_9_out,
       and_10_out, and_11_out, and_12_out, and_13_out, and_14_out, and_15_out, and_16_out, and_17_out,
       and_18_out, and_19_out, and_20_out, and_21_out, and_22_out, and_23_out, and_24_out, and_25_out,
       and_26_out, and_27_out, and_28_out, and_29_out, and_30_out, and_31_out, and_32_out, and_33_out,
       and_34_out, and_35_out, and_36_out, and_37_out, and_38_out, and_39_out, and_40_out, and_41_out,
       and_42_out, and_43_out, d_ff_as_1_nq, d_ff_as_2_nq, d_ff_as_3_nq, d_ff_as_4_nq, d_ff_as_5_nq,
       d_ff_as_6_nq, d_ff_as_7_nq, d_ff_as_8_nq, nand_1_out, nand_2_out, nand_3_out, nand_4_out, nand_5_out,
       nand_6_out, nor_1_out, nor_2_out, nor_3_out, nor_4_out, nor_5_out, nor_6_out, nor_7_out, nor_8_out,
       nor_9_out, nor_10_out, nor_11_out, nor_12_out, nor_13_out, nor_14_out, nor_15_out, nor_16_out,
       not_1_out, not_2_out, not_3_out, not_4_out, not_5_out, not_6_out, not_7_out, not_8_out;

  not not_1 (not_1_out, S0);
  not not_2 (not_2_out, S1);
  not not_3 (not_3_out, CLK);
  not not_4 (not_4_out, not_1_out);
  and and_1 (and_1_out, ~not_1_out, ~nENT);  // And
  and and_2 (and_2_out, ~not_1_out, ~nENT, ~nENP);  // And
  not not_5 (not_5_out, not_2_out);
  and and_3 (and_3_out, not_1_out, ~not_2_out);  // And
  nand nand_1 (nand_1_out, nor_9_out, and_2_out);
  nand nand_2 (nand_2_out, nor_10_out, nor_9_out, and_2_out);
  nand nand_3 (nand_3_out, nor_11_out, nor_10_out, nor_9_out, and_2_out);
  nand nand_4 (nand_4_out, nor_12_out, nor_11_out, nor_10_out, nor_9_out, and_2_out);
  not not_6 (not_6_out, and_2_out);
  not not_7 (not_7_out, nand_4_out);
  not not_8 (not_8_out, nor_13_out);
  nand nand_5 (nand_5_out, nor_14_out, nor_13_out);
  nand nand_6 (nand_6_out, nor_15_out, nor_14_out, nor_13_out);
  and and_4 (and_4_out, Q_A, not_6_out, not_4_out);
  and and_5 (and_5_out, and_3_out, A);
  and and_6 (and_6_out, and_2_out, d_ff_as_1_nq);
  and and_7 (and_7_out, Q_B, nand_1_out, not_4_out);
  and and_8 (and_8_out, and_3_out, B);
  and and_9 (and_9_out, nor_9_out, and_2_out, d_ff_as_2_nq);
  and and_10 (and_10_out, Q_C, nand_2_out, not_4_out);
  and and_11 (and_11_out, and_3_out, C);
  and and_12 (and_12_out, nor_10_out, nor_9_out, and_2_out, d_ff_as_3_nq);
  and and_13 (and_13_out, Q_D, nand_3_out, not_4_out);
  and and_14 (and_14_out, and_3_out, D);
  and and_15 (and_15_out, nor_11_out, nor_10_out, nor_9_out, and_2_out, d_ff_as_4_nq);
  and and_16 (and_16_out, Q_E, nand_4_out, not_4_out);
  and and_17 (and_17_out, and_3_out, E);
  and and_18 (and_18_out, not_7_out, d_ff_as_5_nq);
  and and_19 (and_19_out, Q_F, not_8_out, not_4_out);
  and and_20 (and_20_out, and_3_out, F);
  and and_21 (and_21_out, nor_13_out, d_ff_as_6_nq);
  and and_22 (and_22_out, Q_G, nand_5_out, not_4_out);
  and and_23 (and_23_out, and_3_out, G);
  and and_24 (and_24_out, nor_14_out, nor_13_out, d_ff_as_7_nq);
  and and_25 (and_25_out, Q_H, nand_6_out, not_4_out);
  and and_26 (and_26_out, and_3_out, H);
  and and_27 (and_27_out, nor_15_out, nor_14_out, nor_13_out, d_ff_as_8_nq);
  nor nor_1 (nor_1_out, and_4_out, and_5_out, and_6_out);
  nor nor_2 (nor_2_out, and_7_out, and_8_out, and_9_out);
  nor nor_3 (nor_3_out, and_10_out, and_11_out, and_12_out);
  nor nor_4 (nor_4_out, and_13_out, and_14_out, and_15_out);
  nor nor_5 (nor_5_out, and_16_out, and_17_out, and_18_out);
  nor nor_6 (nor_6_out, and_19_out, and_20_out, and_21_out);
  nor nor_7 (nor_7_out, and_22_out, and_23_out, and_24_out);
  nor nor_8 (nor_8_out, and_25_out, and_26_out, and_27_out);
  D_FF_AS d_ff_as_1 (.Set(1'b0), .D(~nor_1_out), .C(~not_3_out), .Clr(~1'b1), .Q(Q_A), .nQ(d_ff_as_1_nq));
  D_FF_AS d_ff_as_2 (.Set(1'b0), .D(~nor_2_out), .C(~not_3_out), .Clr(~1'b1), .Q(Q_B), .nQ(d_ff_as_2_nq));
  D_FF_AS d_ff_as_3 (.Set(1'b0), .D(~nor_3_out), .C(~not_3_out), .Clr(~1'b1), .Q(Q_C), .nQ(d_ff_as_3_nq));
  D_FF_AS d_ff_as_4 (.Set(1'b0), .D(~nor_4_out), .C(~not_3_out), .Clr(~1'b1), .Q(Q_D), .nQ(d_ff_as_4_nq));
  D_FF_AS d_ff_as_5 (.Set(1'b0), .D(~nor_5_out), .C(~not_3_out), .Clr(~1'b1), .Q(Q_E), .nQ(d_ff_as_5_nq));
  D_FF_AS d_ff_as_6 (.Set(1'b0), .D(~nor_6_out), .C(~not_3_out), .Clr(~1'b1), .Q(Q_F), .nQ(d_ff_as_6_nq));
  D_FF_AS d_ff_as_7 (.Set(1'b0), .D(~nor_7_out), .C(~not_3_out), .Clr(~1'b1), .Q(Q_G), .nQ(d_ff_as_7_nq));
  D_FF_AS d_ff_as_8 (.Set(1'b0), .D(~nor_8_out), .C(~not_3_out), .Clr(~1'b1), .Q(Q_H), .nQ(d_ff_as_8_nq));
  and and_28 (and_28_out, not_2_out, Q_A);
  and and_29 (and_29_out, d_ff_as_1_nq, not_5_out);
  and and_30 (and_30_out, not_2_out, Q_B);
  and and_31 (and_31_out, d_ff_as_2_nq, not_5_out);
  and and_32 (and_32_out, not_2_out, Q_C);
  and and_33 (and_33_out, d_ff_as_3_nq, not_5_out);
  and and_34 (and_34_out, not_2_out, Q_D);
  and and_35 (and_35_out, d_ff_as_4_nq, not_5_out);
  and and_36 (and_36_out, not_2_out, Q_E);
  and and_37 (and_37_out, d_ff_as_5_nq, not_5_out);
  and and_38 (and_38_out, not_2_out, Q_F);
  and and_39 (and_39_out, d_ff_as_6_nq, not_5_out);
  and and_40 (and_40_out, not_2_out, Q_G);
  and and_41 (and_41_out, d_ff_as_7_nq, not_5_out);
  and and_42 (and_42_out, not_2_out, Q_H);
  and and_43 (and_43_out, d_ff_as_8_nq, not_5_out);
  nor nor_9 (nor_9_out, and_28_out, and_29_out);
  nor nor_10 (nor_10_out, and_30_out, and_31_out);
  nor nor_11 (nor_11_out, and_32_out, and_33_out);
  nor nor_12 (nor_12_out, and_34_out, and_35_out);
  nor nor_13 (nor_13_out, nand_4_out, and_36_out, and_37_out);
  nor nor_14 (nor_14_out, and_38_out, and_39_out);
  nor nor_15 (nor_15_out, and_40_out, and_41_out);
  nor nor_16 (nor_16_out, and_42_out, and_43_out);
  nand nand_7 (nRCO, and_1_out, nor_9_out, nor_13_out, nor_14_out, nor_15_out, nor_16_out);

  // Notes on the sheet:
  //   S0: pin 1
  //   S1: pin 2
  //   nENT: pin 11
  //   nENP: pin 23
  //   CLK: pin 14
  //   A: pin 3
  //   H: pin 10
  //   G: pin 9
  //   F: pin 8
  //   E: pin 7
  //   D: pin 6
  //   C: pin 5
  //   B: pin 4
  //   Q_H: pin 15
  //   Q_G: pin 16
  //   Q_F: pin 17
  //   Q_E: pin 18
  //   Q_D: pin 19
  //   Q_C: pin 20
  //   Q_B: pin 21
  //   Q_A: pin 22
  //   nRCO: pin 13
  //   Not connected on 869 (synchronous clear)
endmodule
