// Digital circuit tom-1-283.dig as structural Verilog
module tom_1_283 (
  input  C0,
  input  [3:0] A,
  input  [3:0] B,
  output C4,
  output [3:0] S
);

  _74283 _74283_1 (
    .pin1(S[1]), .pin2(B[1]), .pin3(A[1]), .pin4(S[0]), .pin5(A[0]), .pin6(B[0]), .pin7(C0), .pin8(1'b0),
    .pin9(C4), .pin10(S[3]), .pin11(B[3]), .pin12(A[3]), .pin13(S[2]), .pin14(A[2]), .pin15(B[2]),
    .pin16(1'b1));
endmodule
