// Digital circuit tom-1-573.dig as structural Verilog
module tom_1_573 (
  input  C,
  input  [7:0] in,
  output [7:0] out
);

  _74573 _74573_1 (
    .pin1(1'b0), .pin2(in[0]), .pin3(in[1]), .pin4(in[2]), .pin5(in[3]), .pin6(in[4]), .pin7(in[5]),
    .pin8(in[6]), .pin9(in[7]), .pin10(1'b0), .pin11(C), .pin12(out[7]), .pin13(out[6]), .pin14(out[5]),
    .pin15(out[4]), .pin16(out[3]), .pin17(out[2]), .pin18(out[1]), .pin19(out[0]), .pin20(1'b1));
endmodule
