// Digital circuit tom-1-d_r.dig as structural Verilog
module tom_1_d_r (
  input  nENP,
  input  nCCLR,
  input  RCK,
  input  R_nC,
  input  nG,
  input  nLOAD,
  input  nENT,
  input  U_nD,
  input  [7:0] D,
  input  CCK,
  output [7:0] Q
);

  wire _74697_1_nrco;

  _74697 _74697_1 (
    .CCK(CCK), .nENT(nENT), .nENP(nENP), .nLOAD(nLOAD), .U_nD(U_nD), .nCCLR(nCCLR), .RCK(RCK), .R_nC(R_nC),
    .nG(nG), .A(D[0]), .B(D[1]), .C(D[2]), .D(D[3]), .Qa(Q[0]), .Qb(Q[1]), .Qc(Q[2]), .Qd(Q[3]),
    .nRCO(_74697_1_nrco), .VCC(1'b1), .GND(1'b0));
  _74697 _74697_2 (
    .CCK(CCK), .nENT(_74697_1_nrco), .nENP(nENP), .nLOAD(nLOAD), .U_nD(U_nD), .nCCLR(nCCLR), .RCK(RCK),
    .R_nC(R_nC), .nG(nG), .A(D[4]), .B(D[5]), .C(D[6]), .D(D[7]), .Qa(Q[4]), .Qb(Q[5]), .Qc(Q[6]), .Qd(Q[7]),
    .VCC(1'b1), .GND(1'b0));  // open: nRCO

  // Notes on the sheet:
  //   nCCLR: default 1
  //   nG: default 1
  //   nLOAD: default 1
  //   U_nD: default 1
endmodule
