// Digital circuit tom-1-nand.dig as structural Verilog
module tom_1_nand (
  input  [15:0] A,
  input  [15:0] B,
  input  enable,
  output [15:0] out
);

  wire [3:0] _7400_3_pin6, _7400_4_pin6;
  wire [7:0] _7400_1_pin6;

  _7400 _7400_1 (
    .pin1(A[0]), .pin2(B[0]), .pin3(_7400_1_pin6[0]), .pin4(A[1]), .pin5(B[1]), .pin6(_7400_1_pin6[1]),
    .pin7(1'b0), .pin8(_7400_1_pin6[2]), .pin9(A[2]), .pin10(B[2]), .pin11(_7400_1_pin6[3]), .pin12(A[3]),
    .pin13(B[3]), .pin14(1'b1));
  _7400 _7400_2 (
    .pin1(A[4]), .pin2(B[4]), .pin3(_7400_1_pin6[4]), .pin4(A[5]), .pin5(B[5]), .pin6(_7400_1_pin6[5]),
    .pin7(1'b0), .pin8(_7400_1_pin6[6]), .pin9(A[6]), .pin10(B[6]), .pin11(_7400_1_pin6[7]), .pin12(A[7]),
    .pin13(B[7]), .pin14(1'b1));
  _7400 _7400_3 (
    .pin1(A[8]), .pin2(B[8]), .pin3(_7400_3_pin6[0]), .pin4(A[9]), .pin5(B[9]), .pin6(_7400_3_pin6[1]),
    .pin7(1'b0), .pin8(_7400_3_pin6[2]), .pin9(A[10]), .pin10(B[10]), .pin11(_7400_3_pin6[3]), .pin12(A[11]),
    .pin13(B[11]), .pin14(1'b1));
  _7400 _7400_4 (
    .pin1(A[12]), .pin2(B[12]), .pin3(_7400_4_pin6[0]), .pin4(A[13]), .pin5(B[13]), .pin6(_7400_4_pin6[1]),
    .pin7(1'b0), .pin8(_7400_4_pin6[2]), .pin9(A[14]), .pin10(B[14]), .pin11(_7400_4_pin6[3]), .pin12(A[15]),
    .pin13(B[15]), .pin14(1'b1));
  assign out = enable ? {_7400_4_pin6, _7400_3_pin6, _7400_1_pin6} : 16'bz;  // Driver driver_1
endmodule
