// Digital circuit tom-1-pc.dig as structural Verilog
module tom_1_pc (
  input  clk,
  input  [15:0] \input ,
  input  nLOAD,
  output [15:0] pc
);

  wire _74191_1_pin13, _74191_2_pin13, _74191_3_pin13;

  _74191 _74191_1 (
    .pin1(\input [1]), .pin2(pc[1]), .pin3(pc[0]), .pin4(1'b0), .pin5(1'b0), .pin6(pc[2]), .pin7(pc[3]),
    .pin8(1'b0), .pin9(\input [3]), .pin10(\input [2]), .pin11(nLOAD), .pin13(_74191_1_pin13), .pin14(clk),
    .pin15(\input [0]), .pin16(1'b1));  // open: pin12
  _74191 _74191_2 (
    .pin1(\input [5]), .pin2(pc[5]), .pin3(pc[4]), .pin4(_74191_1_pin13), .pin5(1'b0), .pin6(pc[6]),
    .pin7(pc[7]), .pin8(1'b0), .pin9(\input [7]), .pin10(\input [6]), .pin11(nLOAD), .pin13(_74191_2_pin13),
    .pin14(clk), .pin15(\input [4]), .pin16(1'b1));  // open: pin12
  _74191 _74191_3 (
    .pin1(\input [9]), .pin2(pc[9]), .pin3(pc[8]), .pin4(_74191_2_pin13), .pin5(1'b0), .pin6(pc[10]),
    .pin7(pc[11]), .pin8(1'b0), .pin9(\input [11]), .pin10(\input [10]), .pin11(nLOAD),
    .pin13(_74191_3_pin13), .pin14(clk), .pin15(\input [8]), .pin16(1'b1));  // open: pin12
  _74191 _74191_4 (
    .pin1(\input [13]), .pin2(pc[13]), .pin3(pc[12]), .pin4(_74191_3_pin13), .pin5(1'b0), .pin6(pc[14]),
    .pin7(pc[15]), .pin8(1'b0), .pin9(\input [15]), .pin10(\input [14]), .pin11(nLOAD), .pin14(clk),
    .pin15(\input [12]), .pin16(1'b1));  // open: pin12, pin13
  LED led_1 (.in(pc[3]));
  LED led_2 (.in(pc[2]));
  LED led_3 (.in(pc[1]));
  LED led_4 (.in(pc[0]));
  LED led_5 (.in(pc[7]));
  LED led_6 (.in(pc[6]));
  LED led_7 (.in(pc[5]));
  LED led_8 (.in(pc[4]));
  LED led_9 (.in(pc[11]));
  LED led_10 (.in(pc[10]));
  LED led_11 (.in(pc[9]));
  LED led_12 (.in(pc[8]));
  LED led_13 (.in(pc[15]));
  LED led_14 (.in(pc[14]));
  LED led_15 (.in(pc[13]));
  LED led_16 (.in(pc[12]));
endmodule
