// Digital circuit tom-139.dig as structural Verilog
module tom_139 (
  input  _1A,
  input  _1B,
  input  _2A,
  input  _2B,
  output [3:0] _1C,
  output [3:0] _2C
);

  _74139 _74139_1 (
    .pin1(1'b0), .pin2(_1A), .pin3(_1B), .pin4(_1C[0]), .pin5(_1C[1]), .pin6(_1C[2]), .pin7(_1C[3]),
    .pin8(1'b0), .pin9(_2C[3]), .pin10(_2C[2]), .pin11(_2C[1]), .pin12(_2C[0]), .pin13(_2B), .pin14(_2A),
    .pin15(1'b0), .pin16(1'b1));
endmodule
