// Digital circuit tom-373.dig as structural Verilog
module tom_373 (
  input  nOC,
  input  [7:0] D,
  input  CLK,
  output [7:0] Q
);

  _74373 _74373_1 (
    .pin1(nOC), .pin2(Q[0]), .pin3(D[0]), .pin4(D[1]), .pin5(Q[1]), .pin6(Q[2]), .pin7(D[2]), .pin8(D[3]),
    .pin9(Q[3]), .pin10(1'b0), .pin11(CLK), .pin12(Q[4]), .pin13(D[4]), .pin14(D[5]), .pin15(Q[5]),
    .pin16(Q[6]), .pin17(D[6]), .pin18(D[7]), .pin19(Q[7]), .pin20(1'b1));
endmodule
