// Digital circuit tom-543.dig as structural Verilog
module tom_543 (
  input  [7:0] A,
  input  nCEAB,
  input  nOEAB,
  input  nLEAB,
  input  [7:0] B,
  input  nCEBA,
  input  nOEBA,
  input  nLEBA
);

  wire bussplitter_1_d0, bussplitter_1_d1, bussplitter_1_d2, bussplitter_1_d3, bussplitter_1_d4,
       bussplitter_1_d5, bussplitter_1_d6, bussplitter_1_d7, bussplitter_2_d0, bussplitter_2_d1,
       bussplitter_2_d2, bussplitter_2_d3, bussplitter_2_d4, bussplitter_2_d5, bussplitter_2_d6,
       bussplitter_2_d7, not_1_out, not_2_out;

  BusSplitter #(.Bits(8)) bussplitter_1 (
    .D(A), .OE(not_2_out), .D0(bussplitter_1_d0), .D1(bussplitter_1_d1), .D2(bussplitter_1_d2),
    .D3(bussplitter_1_d3), .D4(bussplitter_1_d4), .D5(bussplitter_1_d5), .D6(bussplitter_1_d6),
    .D7(bussplitter_1_d7));
  not not_1 (not_1_out, nOEBA);
  not not_2 (not_2_out, nOEAB);
  BusSplitter #(.Bits(8)) bussplitter_2 (
    .D(B), .OE(not_1_out), .D0(bussplitter_2_d0), .D1(bussplitter_2_d1), .D2(bussplitter_2_d2),
    .D3(bussplitter_2_d3), .D4(bussplitter_2_d4), .D5(bussplitter_2_d5), .D6(bussplitter_2_d6),
    .D7(bussplitter_2_d7));
  _74543 _74543_1 (
    .B1(bussplitter_2_d0), .A1(bussplitter_1_d0), .B2(bussplitter_2_d1), .A2(bussplitter_1_d1),
    .B3(bussplitter_2_d2), .A3(bussplitter_1_d2), .B4(bussplitter_2_d3), .A4(bussplitter_1_d3),
    .B5(bussplitter_2_d4), .A5(bussplitter_1_d4), .B6(bussplitter_2_d5), .A6(bussplitter_1_d5),
    .B7(bussplitter_2_d6), .A7(bussplitter_1_d6), .B8(bussplitter_2_d7), .A8(bussplitter_1_d7),
    .nOEBA(nOEBA), .nCEBA(nCEBA), .nLEBA(nLEBA), .nOEAB(nOEAB), .nCEAB(nCEAB), .nLEAB(nLEAB));

  // Notes on the sheet:
  //   A: pin 1
  //   nCEAB: pin 2
  //   nOEAB: pin 3
  //   nLEAB: pin 4
  //   B: pin 5
  //   nCEBA: pin 6
  //   nOEBA: pin 7
  //   nLEBA: pin 8
endmodule
